// Logisim project cpu.circ as structural Verilog: 1 circuit, main circuit cpu
module cpu (
  input  clk,
  input  [31:0] INSTRUCTION,
  input  [31:0] READ_DATA,
  output [31:0] WRITE_ADDRESS,
  output [31:0] PROGRAM_COUNTER,
  output [31:0] ra,
  output [31:0] sp,
  output [31:0] t0,
  output [31:0] t1,
  output [31:0] t2,
  output [31:0] s0,
  output [31:0] s1,
  output [31:0] a0,
  output [31:0] tohost,
  output [3:0] WRITE_ENABLE,
  output [31:0] WRITE_DATA
);

  wire [3:0] undriven;
  wire [4:0] rs2;
  wire [31:0] fetch_addr, imm, INSTRUCTION_ID, multiplexer_1_out, RegWriteData, rs1_value;

  Register #(.width(32)) IR (.D(INSTRUCTION), .en(1'b1), .clk(clk), .Q(INSTRUCTION_ID));  // open: clr
  Adder #(.width(32)) adder_1 (.a(PROGRAM_COUNTER), .b(32'h4), .out(fetch_addr));  // open: cin, cout
  Register #(.width(32)) PC (.D(fetch_addr), .clk(clk), .Q(PROGRAM_COUNTER));  // open: en, clr
  // control_logic control_logic_1: pin names not known
  imm_gen imm_gen_1 (.inst(INSTRUCTION_ID), .imm(imm));  // open: ImmSel
  regfile regfile_1 (
    .rs1(INSTRUCTION_ID[19:15]), .rs2(rs2), .rd(INSTRUCTION_ID[11:7]), .Write_Data(RegWriteData),
    .RegWEn(1'b1), .clk(clk), .ra(ra), .sp(sp), .t0(t0), .t1(t1), .t2(t2), .s0(s0), .s1(s1), .a0(a0),
    .Read_Data_1(rs1_value), .Read_Data_2(WRITE_DATA));
  // branch_comp branch_comp_1: pin names not known
  Multiplexer #(.enable("false"), .width(32)) multiplexer_1 (
    .in0(WRITE_DATA), .in1(imm), .out(multiplexer_1_out), .sel(1'b1));
  alu alu_1 (.Result(WRITE_ADDRESS), .A(rs1_value), .B(multiplexer_1_out), .ALUSel(undriven));
  csr csr_1 (.CSR_address(12'h51e), .clk(clk), .tohost(tohost));  // open: CSR_din, CSR_WE
  Multiplexer #(.enable("false"), .select(2), .width(32)) multiplexer_2 (
    .in0(READ_DATA), .in1(WRITE_ADDRESS), .out(RegWriteData), .sel(2'b01));  // open: in2, in3

  // Other names for the same wires on the sheet: alu_result[31:0] = WRITE_ADDRESS; rd[4:0] = INSTRUCTION_ID[11:7];
  //   rs1[4:0] = INSTRUCTION_ID[19:15]; rs2_value[31:0] = WRITE_DATA

  // Notes on the sheet:
  //   Output to IMEM
  //   IMEM (do **NOT** move this)
  //   Inputs from IMEM
  //   It is OK to move the PC, RegFile, ALU, MEM, Branch Comp, Imm Gen, and Control Logic to wherever is most convenient for you when constructing your CPU, and to delete this text
  //   Inputs/Outputs for testing. Do **NOT** move these.
  //   Outputs To DMEM
  //   DMEM (do **NOT** move this)
  //   Inputs From DMEM
endmodule
